// Logisim project cpu.circ as structural Verilog: 4 circuits, main circuit main
module main (
);

  // CPU cpu_1: pin names not known
endmodule

module CPU (
  input  in_1
);
endmodule

module Control (
  input  [31:0] in_1
);


  // Other names for the same wires on the sheet: OpCode[6:0] = in_1[6:0]; imm4_0[4:0] = in_1[11:7];
  //   rd[4:0] = in_1[11:7]; funct3[2:0] = in_1[14:12]; imm31_12[19:0] = in_1[31:12]; rs1[4:0] = in_1[19:15];
  //   rs2[4:0] = in_1[24:20]; imm11_0[10:0] = in_1[31:21]; funct7[6:0] = in_1[31:25]
endmodule

module PC (
);

  Register register_1 ();  // open: D, en, Q, clk, clr
  Adder #(.width(32)) adder_1 ();  // open: a, b, out, cin, cout
endmodule
